// Logisim project Assignment_1_Le_Quang_Hai.circ as structural Verilog: 8 circuits, main circuit main
module main (
);

  wire alarm_engine_1_out_9, and_1_out, and_2_out, and_3_out, and_4_out, and_5_out, and_6_out, clock_1_out,
       enable_alarm_out, hour_1_alarm_noise, hour_1_am_pm, increment_hour_out, increment_minute_out,
       j_k_ff_1_q, j_k_ff_1_qn, j_k_ff_2_q, j_k_ff_2_qn, j_k_ff_3_q, minute_1_alarm_noise,
       minute_1_increment, not_1_out, not_2_out, or_1_out, reset_out, set_alarm_out, set_time_out,
       swap_AM_PM_out, xor_1_out;
  wire [3:0] hour_1_least_sig, hour_1_out_11, minute_1_least_sig, minute_1_out_10;

  Clock clock_1 (.out(clock_1_out));
  Button set_time (.out(set_time_out));
  Button set_alarm (.out(set_alarm_out));
  Button reset (.out(reset_out));
  Button increment_minute (.out(increment_minute_out));
  Button increment_hour (.out(increment_hour_out));
  Button swap_AM_PM (.out(swap_AM_PM_out));
  J_K_Flip_Flop #(.trigger("falling")) j_k_ff_1 (
    .J(not_2_out), .K(not_2_out), .clk(and_1_out), .Q(j_k_ff_1_q), .Qn(j_k_ff_1_qn), .reset(reset_out));  // open: preset
  and and_1 (and_1_out, set_time_out, j_k_ff_2_qn);
  J_K_Flip_Flop #(.trigger("falling")) j_k_ff_2 (
    .J(not_2_out), .K(not_2_out), .clk(and_2_out), .Q(j_k_ff_2_q), .Qn(j_k_ff_2_qn), .reset(reset_out));  // open: preset
  and and_2 (and_2_out, j_k_ff_1_qn, set_alarm_out);
  J_K_Flip_Flop #(.trigger("falling")) j_k_ff_3 (
    .J(not_2_out), .K(not_2_out), .clk(enable_alarm_out), .Q(j_k_ff_3_q), .reset(reset_out));  // open: Qn, preset
  Button enable_alarm (.out(enable_alarm_out));
  or or_1 (or_1_out, and_2_out, enable_alarm_out);
  and and_3 (and_3_out, clock_1_out, not_1_out);
  not not_1 (not_1_out, xor_1_out);
  not not_2 (not_2_out, reset_out);
  and and_4 (and_4_out, xor_1_out, increment_minute_out);
  and and_5 (and_5_out, xor_1_out, increment_hour_out);
  and and_6 (and_6_out, xor_1_out, swap_AM_PM_out);
  xor xor_1 (xor_1_out, j_k_ff_1_q, j_k_ff_2_q);
  Hex_Digit_Display hex_digit_display_1 (.value(hour_1_out_11));  // open: dp
  Hex_Digit_Display hex_digit_display_2 (.value(hour_1_least_sig));  // open: dp
  Hex_Digit_Display hex_digit_display_3 (.value(minute_1_out_10));  // open: dp
  Hex_Digit_Display hex_digit_display_4 (.value(minute_1_least_sig));  // open: dp
  minute minute_1 (
    .clock(and_3_out), .control(not_2_out), .reset(reset_out), .add_one(and_4_out), .set_alarm(and_2_out),
    .least_sig(minute_1_least_sig[0]), .out_7(minute_1_least_sig[1]), .out_8(minute_1_least_sig[2]),
    .out_9(minute_1_least_sig[3]), .out_10(minute_1_out_10[0]), .out_11(minute_1_out_10[1]),
    .out_12(minute_1_out_10[2]), .most_sig(minute_1_out_10[3]), .increment(minute_1_increment),
    .alarm_noise(minute_1_alarm_noise));
  hour hour_1 (
    .clock(minute_1_increment), .control(not_2_out), .reset(reset_out), .add_one(and_5_out),
    .swap_AM_PM(and_6_out), .set_alarm(and_2_out), .least_sig(hour_1_least_sig[0]),
    .out_8(hour_1_least_sig[1]), .out_9(hour_1_least_sig[2]), .out_10(hour_1_least_sig[3]),
    .out_11(hour_1_out_11[0]), .out_12(hour_1_out_11[1]), .out_13(hour_1_out_11[2]),
    .out_14(hour_1_out_11[3]), .AM_PM(hour_1_am_pm), .alarm_noise(hour_1_alarm_noise));
  LED led_1 (.in(hour_1_am_pm));
  alarm_engine alarm_engine_1 (
    .minute(minute_1_alarm_noise), .hour(hour_1_alarm_noise), .reset(reset_out), .control(not_2_out),
    .stop(or_1_out), .enable(j_k_ff_3_q), .is_set(j_k_ff_2_qn), .clock(and_3_out),
    .out_9(alarm_engine_1_out_9));
  LED alarm_noise (.in(alarm_engine_1_out_9));

  // Notes on the sheet:
  //   clock
  //   in set time or alarm mode !
  //   in set time or alarm mode !
  //   in alarm mode !
  //   off: AM
  //   on: PM
endmodule

module mod_ten_sync_counter (
  input  control,
  input  clock,
  input  reset,
  input  add_one,
  input  back_to_1,
  input  least,
  input  in_7,
  input  in_8,
  input  most,
  input  set_to_value,
  output least_sig,
  output out_12,
  output out_13,
  output most_sig,
  output increment,
  output alarm_noise
);

  wire and_1_out, and_2_out, and_3_out, and_4_out, and_5_out, and_6_out, and_7_out, and_8_out, and_9_out,
       and_10_out, eight_out, four_out, j_k_ff_1_q, j_k_ff_2_q, j_k_ff_3_q, j_k_ff_4_q, nine_out, not_1_out,
       not_2_out, not_3_out, not_4_out, not_5_out, not_6_out, one_out, or_1_out, or_2_out, or_3_out,
       or_4_out, or_5_out, or_6_out, six_out, three_out, two_out, xnor_1_out, xnor_2_out, xnor_3_out,
       xnor_4_out, xor_1_out;

  xor six (six_out, clock, add_one);
  or eight (eight_out, reset, back_to_1);
  and and_1 (and_1_out, most, set_to_value);
  xor xor_1 (xor_1_out, six_out, set_to_value);
  and and_2 (and_2_out, in_8, set_to_value);
  or or_1 (or_1_out, xor_1_out, eight_out);
  not not_1 (not_1_out, or_1_out);
  and and_3 (and_3_out, in_7, set_to_value);
  and and_4 (and_4_out, least, set_to_value);
  or or_2 (or_2_out, back_to_1, and_4_out);
  J_K_Flip_Flop #(.trigger("falling")) j_k_ff_1 (
    .J(control), .K(control), .clk(not_2_out), .Q(j_k_ff_1_q), .preset(or_2_out), .reset(or_3_out));  // open: Qn
  not not_2 (not_2_out, not_1_out);
  or or_3 (or_3_out, and_5_out, reset);
  and and_5 (and_5_out, not_3_out, set_to_value);
  not not_3 (not_3_out, least);
  J_K_Flip_Flop #(.trigger("falling")) j_k_ff_2 (
    .J(j_k_ff_1_q), .K(j_k_ff_1_q), .clk(not_2_out), .Q(j_k_ff_2_q), .preset(and_3_out), .reset(or_4_out));  // open: Qn
  and and_6 (and_6_out, not_4_out, set_to_value);
  not not_4 (not_4_out, in_7);
  and one (one_out, j_k_ff_1_q, j_k_ff_2_q);
  or or_4 (or_4_out, and_6_out, nine_out);
  J_K_Flip_Flop #(.trigger("falling")) j_k_ff_3 (
    .J(one_out), .K(one_out), .clk(not_2_out), .Q(j_k_ff_3_q), .preset(and_2_out), .reset(or_5_out));  // open: Qn
  or or_5 (or_5_out, and_7_out, nine_out);
  and and_7 (and_7_out, not_5_out, set_to_value);
  not not_5 (not_5_out, in_8);
  and two (two_out, one_out, j_k_ff_3_q);
  J_K_Flip_Flop #(.trigger("falling")) j_k_ff_4 (
    .J(two_out), .K(two_out), .clk(not_2_out), .Q(j_k_ff_4_q), .preset(and_1_out), .reset(or_6_out));  // open: Qn
  or or_6 (or_6_out, and_8_out, nine_out);
  and and_8 (and_8_out, not_6_out, set_to_value);
  not not_6 (not_6_out, most);
  or nine (nine_out, eight_out, three_out);
  and three (three_out, j_k_ff_2_q, j_k_ff_4_q);
  and four (four_out, j_k_ff_4_q, j_k_ff_1_q);
  D_Flip_Flop #(.trigger("falling")) d_ff_1 (
    .D(j_k_ff_1_q), .clk(not_2_out), .Q(least_sig), .reset(reset));  // open: Qn, preset
  D_Flip_Flop #(.trigger("falling")) d_ff_2 (
    .D(j_k_ff_2_q), .clk(not_2_out), .Q(out_12), .reset(reset));  // open: Qn, preset
  D_Flip_Flop #(.trigger("falling")) d_ff_3 (
    .D(j_k_ff_3_q), .clk(not_2_out), .Q(out_13), .reset(reset));  // open: Qn, preset
  D_Flip_Flop #(.trigger("falling")) d_ff_4 (
    .D(j_k_ff_4_q), .clk(not_2_out), .Q(most_sig), .reset(reset));  // open: Qn, preset
  D_Flip_Flop #(.trigger("falling")) d_ff_5 (
    .D(four_out), .clk(not_2_out), .Q(increment), .reset(reset));  // open: Qn, preset
  xnor xnor_1 (xnor_1_out, least_sig, least);
  xnor xnor_2 (xnor_2_out, out_12, in_7);
  xnor xnor_3 (xnor_3_out, out_13, in_8);
  xnor xnor_4 (xnor_4_out, most_sig, most);
  and and_9 (and_9_out, xnor_1_out, xnor_2_out);
  and and_10 (and_10_out, xnor_3_out, xnor_4_out);
  and and_11 (alarm_noise, and_9_out, and_10_out);

  // Notes on the sheet:
  //   assign value from register to the counter
  //   compare if current time
  //   == alarm time in register
endmodule

module mod_six_sync_counter (
  input  control,
  input  clock,
  input  reset,
  input  least,
  input  in_5,
  input  in_6,
  input  set_to_value,
  output least_sig,
  output out_9,
  output out_10,
  output most_sig,
  output increment,
  output alarm_noise
);

  wire and_1_out, and_2_out, and_3_out, and_4_out, and_5_out, and_6_out, and_7_out, and_8_out, and_10_out,
       and_11_out, j_k_ff_1_q, j_k_ff_2_q, j_k_ff_3_q, not_1_out, not_2_out, not_3_out, not_4_out, not_5_out,
       not_6_out, or_1_out, or_2_out, or_3_out, or_4_out, or_5_out, xnor_1_out, xnor_2_out, xnor_3_out,
       xor_1_out;

  or or_1 (or_1_out, clock, reset);
  xor xor_1 (xor_1_out, or_1_out, set_to_value);
  and and_1 (and_1_out, in_6, set_to_value);
  not not_1 (not_1_out, xor_1_out);
  and and_2 (and_2_out, in_5, set_to_value);
  not not_2 (not_2_out, not_1_out);
  and and_3 (and_3_out, least, set_to_value);
  not not_3 (not_3_out, least);
  J_K_Flip_Flop #(.trigger("falling")) j_k_ff_1 (
    .J(control), .K(control), .clk(not_2_out), .Q(j_k_ff_1_q), .preset(and_3_out), .reset(or_2_out));  // open: Qn
  or or_2 (or_2_out, and_4_out, or_5_out);
  and and_4 (and_4_out, not_3_out, set_to_value);
  J_K_Flip_Flop #(.trigger("falling")) j_k_ff_2 (
    .J(j_k_ff_1_q), .K(j_k_ff_1_q), .clk(not_2_out), .Q(j_k_ff_2_q), .preset(and_2_out), .reset(or_3_out));  // open: Qn
  or or_3 (or_3_out, and_5_out, or_5_out);
  and and_5 (and_5_out, not_4_out, set_to_value);
  not not_4 (not_4_out, in_5);
  and and_6 (and_6_out, j_k_ff_1_q, j_k_ff_2_q);
  J_K_Flip_Flop #(.trigger("falling")) j_k_ff_3 (
    .J(and_6_out), .K(and_6_out), .clk(not_2_out), .Q(j_k_ff_3_q), .preset(and_1_out), .reset(or_4_out));  // open: Qn
  or or_4 (or_4_out, and_7_out, or_5_out);
  and and_7 (and_7_out, not_5_out, set_to_value);
  not not_5 (not_5_out, in_6);
  and and_8 (and_8_out, j_k_ff_3_q, j_k_ff_2_q);
  or or_5 (or_5_out, and_8_out, reset);
  D_Flip_Flop #(.trigger("falling")) d_ff_1 (
    .D(j_k_ff_1_q), .clk(not_2_out), .Q(least_sig), .reset(reset));  // open: Qn, preset
  D_Flip_Flop #(.trigger("falling")) d_ff_2 (
    .D(j_k_ff_2_q), .clk(not_2_out), .Q(out_9), .reset(reset));  // open: Qn, preset
  D_Flip_Flop #(.trigger("falling")) d_ff_3 (
    .D(j_k_ff_3_q), .clk(not_2_out), .Q(out_10), .reset(reset));  // open: Qn, preset
  not not_6 (not_6_out, reset);
  and and_9 (most_sig, not_6_out, reset);
  D_Flip_Flop #(.trigger("falling")) d_ff_4 (
    .D(and_10_out), .clk(not_2_out), .Q(increment), .reset(reset));  // open: Qn, preset
  and and_10 (and_10_out, j_k_ff_1_q, j_k_ff_3_q);
  xnor xnor_1 (xnor_1_out, least_sig, least);
  xnor xnor_2 (xnor_2_out, out_9, in_5);
  xnor xnor_3 (xnor_3_out, out_10, in_6);
  and and_11 (and_11_out, xnor_2_out, xnor_3_out);
  and and_12 (alarm_noise, xnor_1_out, and_11_out);

  // Notes on the sheet:
  //   assign value from register to the counter
  //   compare if the current value == alarming time in register
endmodule

module minute (
  input  clock,
  input  control,
  input  reset,
  input  add_one,
  input  set_alarm,
  output least_sig,
  output out_7,
  output out_8,
  output out_9,
  output out_10,
  output out_11,
  output out_12,
  output most_sig,
  output increment,
  output alarm_noise
);

  wire alarm_register_1_least_significant, alarm_register_1_most_or_pm_am, alarm_register_1_out_11,
       alarm_register_1_out_12, alarm_register_1_out_13, alarm_register_1_out_14, alarm_register_1_out_15,
       and_1_out, d_ff_1_q, j_k_ff_1_q, not_1_out, tens_digit_alarm_noise, units_digit_alarm_noise,
       units_digit_increment;

  J_K_Flip_Flop #(.trigger("falling")) j_k_ff_1 (
    .J(control), .K(control), .clk(set_alarm), .Q(j_k_ff_1_q), .reset(reset));  // open: Qn, preset
  D_Flip_Flop #(.trigger("falling")) d_ff_1 (
    .D(not_1_out), .clk(set_alarm), .Q(d_ff_1_q), .reset(reset));  // open: Qn, preset
  not not_1 (not_1_out, j_k_ff_1_q);
  and and_1 (and_1_out, d_ff_1_q, set_alarm);
  mod_ten_sync_counter units_digit (
    .control(control), .clock(clock), .reset(reset), .add_one(add_one),
    .least(alarm_register_1_least_significant), .in_7(alarm_register_1_out_11),
    .in_8(alarm_register_1_out_12), .most(alarm_register_1_out_13), .set_to_value(and_1_out),
    .least_sig(least_sig), .out_12(out_7), .out_13(out_8), .most_sig(out_9),
    .increment(units_digit_increment), .alarm_noise(units_digit_alarm_noise));  // open: back_to_1
  mod_six_sync_counter tens_digit (
    .control(control), .clock(units_digit_increment), .reset(reset), .least(alarm_register_1_out_14),
    .in_5(alarm_register_1_out_15), .in_6(alarm_register_1_most_or_pm_am), .set_to_value(and_1_out),
    .least_sig(out_10), .out_9(out_11), .out_10(out_12), .most_sig(most_sig), .increment(increment),
    .alarm_noise(tens_digit_alarm_noise));
  and and_2 (alarm_noise, units_digit_alarm_noise, tens_digit_alarm_noise);
  alarm_register alarm_register_1 (
    .least_sig(least_sig), .in_2(out_7), .in_3(out_8), .in_4(out_9), .in_5(out_10), .in_6(out_11),
    .most_or_AM_PM(out_12), .clock(set_alarm), .reset(reset),
    .least_significant(alarm_register_1_least_significant), .out_11(alarm_register_1_out_11),
    .out_12(alarm_register_1_out_12), .out_13(alarm_register_1_out_13), .out_14(alarm_register_1_out_14),
    .out_15(alarm_register_1_out_15), .most_or_PM_AM(alarm_register_1_most_or_pm_am));
endmodule

module hour (
  input  clock,
  input  control,
  input  reset,
  input  add_one,
  input  swap_AM_PM,
  input  set_alarm,
  output least_sig,
  output out_8,
  output out_9,
  output out_10,
  output out_11,
  output out_12,
  output out_13,
  output out_14,
  output AM_PM,
  output alarm_noise
);

  wire alarm_register_1_least_significant, alarm_register_1_most_or_pm_am, alarm_register_1_out_11,
       alarm_register_1_out_12, alarm_register_1_out_13, alarm_register_1_out_14, and_1_out, and_2_out,
       and_3_out, d_ff_1_q, d_ff_2_q, j_k_ff_1_qn, mod_ten_sync_counter_1_alarm_noise,
       mod_ten_sync_counter_1_increment, mod_two_counter_am_pm_1_alarm_noise, xor_1_out, xor_2_out;

  xor xor_1 (xor_1_out, and_3_out, and_2_out);
  xor xor_2 (xor_2_out, add_one, clock);
  J_K_Flip_Flop #(.trigger("falling")) j_k_ff_1 (
    .J(control), .K(control), .clk(set_alarm), .Qn(j_k_ff_1_qn), .reset(reset));  // open: Q, preset
  D_Flip_Flop #(.trigger("falling")) d_ff_1 (
    .D(j_k_ff_1_qn), .clk(set_alarm), .Q(d_ff_1_q), .reset(reset));  // open: Qn, preset
  mod_ten_sync_counter mod_ten_sync_counter_1 (
    .control(control), .clock(clock), .reset(reset), .add_one(add_one), .back_to_1(d_ff_2_q),
    .least(alarm_register_1_least_significant), .in_7(alarm_register_1_out_11),
    .in_8(alarm_register_1_out_12), .most(alarm_register_1_out_13), .set_to_value(and_1_out),
    .least_sig(least_sig), .out_12(out_8), .out_13(out_9), .most_sig(out_10),
    .increment(mod_ten_sync_counter_1_increment), .alarm_noise(mod_ten_sync_counter_1_alarm_noise));
  mod_two_counter_AM_PM mod_two_counter_am_pm_1 (
    .clock(mod_ten_sync_counter_1_increment), .control(control), .reset(reset), .back_to_one(d_ff_2_q),
    .set_to_value(and_1_out), .swap_AM_PM(xor_1_out), .PM_AM(alarm_register_1_most_or_pm_am),
    .most_sig(alarm_register_1_out_14), .least_sig(out_11), .out_10(out_12), .out_11(out_13),
    .out_12(out_14), .AM_PM(AM_PM), .alarm_noise(mod_two_counter_am_pm_1_alarm_noise));
  and and_1 (and_1_out, d_ff_1_q, set_alarm);
  and and_2 (and_2_out, swap_AM_PM, d_ff_1_q);
  and and_3 (and_3_out, least_sig, out_11);
  D_Flip_Flop #(.trigger("falling")) d_ff_2 (
    .D(and_3_out), .clk(xor_2_out), .Q(d_ff_2_q), .reset(reset));  // open: Qn, preset
  and and_4 (alarm_noise, mod_two_counter_am_pm_1_alarm_noise, mod_ten_sync_counter_1_alarm_noise);
  alarm_register alarm_register_1 (
    .least_sig(least_sig), .in_2(out_8), .in_3(out_9), .in_4(out_10), .in_5(out_11), .most_or_AM_PM(AM_PM),
    .clock(set_alarm), .reset(reset), .least_significant(alarm_register_1_least_significant),
    .out_11(alarm_register_1_out_11), .out_12(alarm_register_1_out_12), .out_13(alarm_register_1_out_13),
    .out_14(alarm_register_1_out_14), .most_or_PM_AM(alarm_register_1_most_or_pm_am));  // open: in_6, out_15
endmodule

module alarm_register (
  input  least_sig,
  input  in_2,
  input  in_3,
  input  in_4,
  input  in_5,
  input  in_6,
  input  most_or_AM_PM,
  input  clock,
  input  reset,
  output least_significant,
  output out_11,
  output out_12,
  output out_13,
  output out_14,
  output out_15,
  output most_or_PM_AM
);

  D_Flip_Flop #(.trigger("falling")) d_ff_1 (
    .D(least_sig), .clk(clock), .Q(least_significant), .preset(reset));  // open: Qn, reset
  D_Flip_Flop #(.trigger("falling")) d_ff_2 (.D(in_2), .clk(clock), .Q(out_11), .preset(reset));  // open: Qn, reset
  D_Flip_Flop #(.trigger("falling")) d_ff_3 (.D(in_3), .clk(clock), .Q(out_12), .preset(reset));  // open: Qn, reset
  D_Flip_Flop #(.trigger("falling")) d_ff_4 (.D(in_4), .clk(clock), .Q(out_13), .preset(reset));  // open: Qn, reset
  D_Flip_Flop #(.trigger("falling")) d_ff_5 (.D(in_5), .clk(clock), .Q(out_14), .preset(reset));  // open: Qn, reset
  D_Flip_Flop #(.trigger("falling")) d_ff_6 (.D(in_6), .clk(clock), .Q(out_15), .preset(reset));  // open: Qn, reset
  D_Flip_Flop #(.trigger("falling")) d_ff_7 (
    .D(most_or_AM_PM), .clk(clock), .Q(most_or_PM_AM), .preset(reset));  // open: Qn, reset
endmodule

module mod_two_counter_AM_PM (
  input  clock,
  input  control,
  input  reset,
  input  back_to_one,
  input  set_to_value,
  input  swap_AM_PM,
  input  PM_AM,
  input  most_sig,
  output least_sig,
  output out_10,
  output out_11,
  output out_12,
  output AM_PM,
  output alarm_noise
);

  wire and_1_out, and_2_out, and_3_out, and_4_out, j_k_ff_1_q, j_k_ff_2_q, not_1_out, not_2_out, not_3_out,
       or_1_out, or_2_out, or_3_out, or_4_out, or_5_out, xnor_1_out, xnor_2_out, xor_1_out;

  or or_1 (or_1_out, clock, back_to_one);
  or or_2 (or_2_out, reset, set_to_value);
  and and_1 (and_1_out, set_to_value, PM_AM);
  and and_2 (and_2_out, set_to_value, not_1_out);
  not not_1 (not_1_out, PM_AM);
  and and_3 (and_3_out, set_to_value, most_sig);
  and and_4 (and_4_out, set_to_value, not_2_out);
  not not_2 (not_2_out, most_sig);
  xor xor_1 (xor_1_out, or_1_out, or_2_out);
  or or_3 (or_3_out, or_2_out, swap_AM_PM);
  J_K_Flip_Flop #(.trigger("falling")) j_k_ff_1 (
    .J(control), .K(control), .clk(or_3_out), .Q(j_k_ff_1_q), .preset(and_1_out), .reset(or_4_out));  // open: Qn
  or or_4 (or_4_out, and_2_out, reset);
  J_K_Flip_Flop #(.trigger("falling")) j_k_ff_2 (
    .J(control), .K(control), .clk(xor_1_out), .Q(j_k_ff_2_q), .preset(and_3_out), .reset(or_5_out));  // open: Qn
  or or_5 (or_5_out, and_4_out, reset);
  D_Flip_Flop #(.trigger("falling")) d_ff_1 (
    .D(j_k_ff_2_q), .clk(xor_1_out), .Q(least_sig), .reset(reset));  // open: Qn, preset
  D_Flip_Flop #(.trigger("falling")) d_ff_2 (
    .D(j_k_ff_1_q), .clk(or_3_out), .Q(AM_PM), .reset(reset));  // open: Qn, preset
  not not_3 (not_3_out, reset);
  xnor xnor_1 (xnor_1_out, AM_PM, PM_AM);
  xnor xnor_2 (xnor_2_out, least_sig, most_sig);
  and and_5 (out_10, not_3_out, reset);
  and and_6 (alarm_noise, xnor_1_out, xnor_2_out);

  assign out_11 = out_10;
  assign out_12 = out_10;

  // Notes on the sheet:
  //   AM-PM calculator
  //   assign value from register
  //   0 & 1 counter (1-12)
  //   compare with value from register
endmodule

module alarm_engine (
  input  minute,
  input  hour,
  input  reset,
  input  control,
  input  stop,
  input  enable,
  input  is_set,
  input  clock,
  output out_9
);

  wire and_1_out, and_2_out, and_3_out, and_4_out, d_ff_1_q, j_k_ff_1_q, not_1_out, xor_1_out;

  and and_1 (and_1_out, minute, hour);
  D_Flip_Flop d_ff_1 (.D(and_2_out), .clk(clock), .Q(d_ff_1_q), .reset(reset));  // open: Qn, preset
  and and_2 (and_2_out, not_1_out, and_1_out);
  and and_3 (and_3_out, stop, j_k_ff_1_q);
  xor xor_1 (xor_1_out, d_ff_1_q, and_3_out);
  and and_4 (and_4_out, xor_1_out, enable);
  not not_1 (not_1_out, j_k_ff_1_q);
  J_K_Flip_Flop j_k_ff_1 (
    .J(control), .K(control), .clk(and_4_out), .Q(j_k_ff_1_q), .reset(reset));  // open: Qn, preset
  and and_5 (out_9, j_k_ff_1_q, is_set);

  // Notes on the sheet:
  //   this make sure the alarm does not turn off
  //   on the next cycle
endmodule
